# Fritzing sketch Layout (saved by Fritzing 0.9.3b)
breadboards: 1

parts:
  Aduino_Uno_SMD_with_CH340G_(Chinese) = Arduino Uno (Rev3) - ICSP
  Ethernet_Shield_W5100 = Arduino Ethernet Shield (Rev3)
  Adafruit_TSL2561 = Adafruit TSL2561 [part_number="Lux Sensor GY-2561"]
  DHT22_(AM2302) = DHT22 Humidity and Temperature Sensor [part_number="Temperature and humidity sensor"]
  C1 = Ceramic Capacitor [capacitance="100 nF" package="0603 [SMD, multilayer]"]
  LED1 = smd LED [color="Red (633nm)" package="0603 [SMD]"]

nets:
  N1: Aduino_Uno_SMD_with_CH340G_(Chinese).ICSP_MOSI, Aduino_Uno_SMD_with_CH340G_(Chinese).D11_PWM/MOSI, Ethernet_Shield_W5100.PWM_D11
  N2: Aduino_Uno_SMD_with_CH340G_(Chinese).D8, LED1.cathode
  N3: Aduino_Uno_SMD_with_CH340G_(Chinese).D10_PWM/SS, Ethernet_Shield_W5100.ETH_CS
  N4: Aduino_Uno_SMD_with_CH340G_(Chinese).D12/MISO, Ethernet_Shield_W5100.SPI/D12
  N5: Aduino_Uno_SMD_with_CH340G_(Chinese).D13/SCK, Ethernet_Shield_W5100.SPI/D13
  N6: Aduino_Uno_SMD_with_CH340G_(Chinese).A4/SDA, Adafruit_TSL2561.SDA
  N7: Aduino_Uno_SMD_with_CH340G_(Chinese).A5/SCL, Adafruit_TSL2561.SCL
  N8: Aduino_Uno_SMD_with_CH340G_(Chinese).D4, Ethernet_Shield_W5100.SDCS
  N9: Aduino_Uno_SMD_with_CH340G_(Chinese).D7, DHT22_(AM2302).DATA
  N10: Aduino_Uno_SMD_with_CH340G_(Chinese).3V3, LED1.anode
  5V: Aduino_Uno_SMD_with_CH340G_(Chinese).5V, Ethernet_Shield_W5100.5V, Adafruit_TSL2561.VIN, DHT22_(AM2302).VDD
  GND: Aduino_Uno_SMD_with_CH340G_(Chinese).GND, Ethernet_Shield_W5100.GND, Adafruit_TSL2561.GND, DHT22_(AM2302).GND
  N11: C1.0, C1.1

custom parts:
  Adafruit TSL2561: The TSL2561 luminosity sensor is an advanced digital light sensor, ideal for use in a wide range of light situations. Compared to low cost CdS cells, this sensor is more precise, allowing for exact lux calculations and can be configured for different gain/timing ranges to detect light ranges from up to 0.1 - 40,000+ Lux on the fly. The best part of this sensor is that it contains both infrared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
